// Digital circuit 4 bit IR.dig as structural Verilog
module _4_bit_IR (
  input  [3:0] Load,
  input  [1:0] ctrl,
  input  clk,
  output [3:0] \output 
);

  wire [3:0] multiplexer_1_out, not_1_out;

  assign not_1_out = ~4'b0000;  // Not not_1, 4 bits wide
  Multiplexer #(.Bits(4), .Selector_Bits(2)) multiplexer_1 (
    .sel(ctrl), .in_0(\output ), .in_1(Load), .in_2(4'b0000), .in_3(not_1_out), .out(multiplexer_1_out));
  _4_bit_register _4_bit_register_1 (.CTRL(ctrl), .CLK(clk), .\input (multiplexer_1_out), .\output (\output ));
endmodule
