// Digital circuit 4 bit PC.dig as structural Verilog
module _4_bit_PC (
  input  [1:0] CTRL,
  input  CLK,
  output [3:0] \output 
);

  wire [3:0] _4_bit_adder_1_sum, multiplexer_1_out, not_1_out;

  _4_bit_adder _4_bit_adder_1 (.A(4'b0001), .B(\output ), .Sum(_4_bit_adder_1_sum));  // open: Overflow_flag
  assign not_1_out = ~4'b0000;  // Not not_1, 4 bits wide
  Multiplexer #(.Selector_Bits(2), .Bits(4)) multiplexer_1 (
    .sel(CTRL), .in_0(\output ), .in_1(_4_bit_adder_1_sum), .in_2(4'b0000), .in_3(not_1_out),
    .out(multiplexer_1_out));
  D_FF R3 (.D(multiplexer_1_out[3]), .C(CLK), .Q(\output [3]));  // open: nQ
  D_FF R2 (.D(multiplexer_1_out[2]), .C(CLK), .Q(\output [2]));  // open: nQ
  D_FF R1 (.D(multiplexer_1_out[1]), .C(CLK), .Q(\output [1]));  // open: nQ
  D_FF R0 (.D(multiplexer_1_out[0]), .C(CLK), .Q(\output [0]));  // open: nQ
endmodule
