// Digital circuit 4 bit adder.dig as structural Verilog
module _4_bit_adder (
  input  [3:0] A,
  input  [3:0] B,
  output [3:0] Sum,
  output Overflow_flag
);

  wire full_bit_adder_circuit_assignment_1_1_p3, full_bit_adder_circuit_assignment_1_2_p3,
       full_bit_adder_circuit_assignment_1_3_p3;

  // Full_Bit_adder_Circuit_assignment_1 full_bit_adder_circuit_assignment_1_1: pin names not known; wires that end beside it: B[3], A[3], full_bit_adder_circuit_assignment_1_1_p3, Overflow_flag, Sum[3]
  // Full_Bit_adder_Circuit_assignment_1 full_bit_adder_circuit_assignment_1_2: pin names not known; wires that end beside it: B[2], A[2], full_bit_adder_circuit_assignment_1_2_p3, full_bit_adder_circuit_assignment_1_1_p3, Sum[2]
  // Full_Bit_adder_Circuit_assignment_1 full_bit_adder_circuit_assignment_1_3: pin names not known; wires that end beside it: B[1], A[1], full_bit_adder_circuit_assignment_1_3_p3, full_bit_adder_circuit_assignment_1_2_p3, Sum[1]
  // Full_Bit_adder_Circuit_assignment_1 full_bit_adder_circuit_assignment_1_4: pin names not known; wires that end beside it: B[0], A[0], 1'b0, full_bit_adder_circuit_assignment_1_3_p3, Sum[0]
endmodule
