// Digital circuit 4 bit register.dig as structural Verilog
module _4_bit_register (
  input  [1:0] CTRL,
  input  CLK,
  input  [3:0] \input ,
  output [3:0] \output 
);

  wire [3:0] multiplexer_1_out, not_1_out;

  assign not_1_out = ~4'b0000;  // Not not_1, 4 bits wide
  Multiplexer #(.Selector_Bits(2), .Bits(4)) multiplexer_1 (
    .sel(CTRL), .in_0(\output ), .in_1(\input ), .in_2(4'b0000), .in_3(not_1_out), .out(multiplexer_1_out));
  D_FF R3 (.D(multiplexer_1_out[3]), .C(CLK), .Q(\output [3]));  // open: nQ
  D_FF R2 (.D(multiplexer_1_out[2]), .C(CLK), .Q(\output [2]));  // open: nQ
  D_FF R1 (.D(multiplexer_1_out[1]), .C(CLK), .Q(\output [1]));  // open: nQ
  D_FF R0 (.D(multiplexer_1_out[0]), .C(CLK), .Q(\output [0]));  // open: nQ
endmodule
