// Digital circuit memory.dig as structural Verilog
module memory (
  input  [1:0] address,
  input  [3:0] \input ,
  input  clk,
  input  [1:0] ctrl,
  output [3:0] \output 
);

  wire and_1_out, and_2_out, and_3_out, and_4_out, decoder_1_out_0, decoder_1_out_1, decoder_1_out_2,
       decoder_1_out_3;
  wire [3:0] _4_bit_register_1_output, _4_bit_register_2_output, _4_bit_register_3_output,
       _4_bit_register_4_output;

  Decoder #(.Selector_Bits(2)) decoder_1 (
    .sel(address), .out_0(decoder_1_out_0), .out_1(decoder_1_out_1), .out_2(decoder_1_out_2),
    .out_3(decoder_1_out_3));
  and and_1 (and_1_out, clk, decoder_1_out_0);
  and and_2 (and_2_out, clk, decoder_1_out_1);
  and and_3 (and_3_out, clk, decoder_1_out_2);
  and and_4 (and_4_out, clk, decoder_1_out_3);
  _4_bit_register _4_bit_register_1 (
    .CTRL(ctrl), .CLK(and_1_out), .\input (\input ), .\output (_4_bit_register_1_output));
  _4_bit_register _4_bit_register_2 (
    .CTRL(ctrl), .CLK(and_2_out), .\input (\input ), .\output (_4_bit_register_2_output));
  _4_bit_register _4_bit_register_3 (
    .CTRL(ctrl), .CLK(and_3_out), .\input (\input ), .\output (_4_bit_register_3_output));
  _4_bit_register _4_bit_register_4 (
    .CTRL(ctrl), .CLK(and_4_out), .\input (\input ), .\output (_4_bit_register_4_output));
  Multiplexer #(.Bits(4), .Selector_Bits(2)) multiplexer_1 (
    .sel(address), .in_0(_4_bit_register_1_output), .in_1(_4_bit_register_2_output),
    .in_2(_4_bit_register_3_output), .in_3(_4_bit_register_4_output), .out(\output ));
endmodule
